# Fritzing sketch Rooftop Garden Heat Sensor (saved by Fritzing 0.9.3b)
breadboards: 1

parts:
  Mod1 = Heltec CubeCell Dev-Board Plus [part_number=HTCC-AB02]
  Part1 = Adafruit BME680 [part_number="Adafruit #3660"]  # not connected
  JP2 = Header 1 [package=1x01_offset]  # not connected
  JP3 = Header 1 [package=1x01_offset]
  JP4 = Header 1 [package=1x01_offset]
  JP5 = Header 1 [package=1x01_offset]
  JP6 = Header 1 [package=1x01_offset]  # not connected

nets:
  N1: Mod1.pin_14, Mod1.pin_19, JP3.1
  N2: Mod1.pin_26, JP4.1
  N3: Mod1.pin_27, JP5.1

custom parts:
  Heltec CubeCell Dev-Board Plus: CubeCell is a part of the Heltec LoRa series and incorporates a PSoC 4000 series processor and SX1262 RF transceiver with an integrated CP2102 USB to serial port interface and onboard SHT1.25 battery interface with integrated lithium battery management system, supporting direct solar panel connection. Links: Heltec CubeCell Dev-Board product page Github
